# Fritzing sketch lamprgb (saved by Fritzing 0.9.2b)

parts:
  TRINKET1 = Trinket 5V
  Part1 = 24 NeoPixel Ring [part_number=1586]
  JACK2 = 2.1mm DC Barrel Jack
  Part2 = Adafruit Perma Pi - Small [part_number="Adafruit #1171"]
  U1 = POT [package=pot_alpha_rv16af-20]
  S1 = SPST Switch [package=switch-spdt]

nets:
  N1: TRINKET1.no_name_yet#2, Part1.GND, JACK2.center, Part2.SCL, Part2.GNDSTRIP1, U1.A
  N2: TRINKET1.no_name_yet#6, Part1.VDD, Part2.GPIO17, Part2.A1, Part2.PWRSTRIP1, U1.E, S1.P
  N3: TRINKET1.no_name_yet#7, Part2.+3.3V, Part2.GPIO27, U1.S
  N4: TRINKET1.no_name_yet#8, Part1.IN, Part2.GPIO22
  N5: TRINKET1.no_name_yet#9, Part2.+3.3V_2
  N6: TRINKET1.no_name_yet#10, Part2.MOSI
  N7: JACK2.switch, S1.S

notes:
  On/off switch

custom parts:
  Trinket 5V: Adafruit Trinket 5V
  24 NeoPixel Ring: 24 ultra bright smart LED NeoPixels are arranged in a circle with 2.6" (66mm) outer diameter. The rings are 'chainable' - connect the output pin of one to the input pin of another. Use only one microcontroller pin to control as many as you can chain together! Each LED is addressable as the driver chip is inside the LED. Each one has ~18mA constant current drive so the color will be very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
  2.1mm DC Barrel Jack: 2.1mm DC Barrel Jack with Thru-Hole Connectors (breadboardable)
  Adafruit Perma Pi - Small: We put a PermaProto quarter-sized proto board in a blender with a Pi Cobbler and out emerged this very tasty confection - the PermaProto for Pi! It has the Cobbler baked right in. Simply solder the 2x13 pin header in and you get all the labeled breakouts with tons of prototyping space, power rails, mounting holes and that gorgeous silk. Customers have asked us to carry basic perf-board, but we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
